# Fritzing sketch master module (saved by Fritzing 0.9.3b)
stripboards: 1

parts:
  U1 = POT [package=pot_mammoth]
  IC2 = IC, DIP package, 16 pins [chip_label=4051]  # not connected
  IC3 = IC, DIP package, 16 pins [chip_label=4051]  # not connected
  J1 = male pin header, 12 pins [form="♂ (male)"]
  TRS1 = Audio Jack (TRS) 3.5mm [package="4Ucon 08780 [THT]"]  # not connected
  TRS2 = Audio Jack (TRS) 3.5mm [package="4Ucon 08780 [THT]"]  # not connected
  TRS3 = Audio Jack (TRS) 3.5mm [package="4Ucon 08780 [THT]"]  # not connected

nets:
  N1: U1.S, J1.pin11
  N2: U1.A, J1.pin9
  N3: U1.E, J1.pin12
