# Fritzing sketch module circuit (saved by Fritzing 0.9.3b)
circuit board: 10cm x 5.64444cm
stripboards: 1

parts:
  U1 = POT [package=pot_mammoth]
  U2 = POT [package=pot_mammoth]
  U3 = POT [package=pot_mammoth]
  U4 = POT [package=pot_mammoth]
  U5 = POT [package=pot_mammoth]
  IC1 = IC, DIP package, 16 pins [chip_label="4051 (send)"]  # not connected
  IC2 = IC, DIP package, 16 pins [chip_label="4051 (id)"]  # not connected
  IC3 = IC, DIP package, 16 pins [chip_label="4051 (analog)"]  # not connected
  IC4 = IC, DIP package, 16 pins [chip_label="4051 (rcv)"]  # not connected
  J2 = female pin header, 4 pins [form="♀ (female)"]
  J3 = female pin header, 4 pins [form="♀ (female)"]
  J4 = female pin header, 7 pins [form="♀ (female)"]
  J1 = male pin header, 12 pins [form="♂ (male)"]

nets:
  N1: U1.S, U2.S, U3.S, U4.S, U5.S, J4.pin1, J1.pin12
  N2: U1.E, U2.E, U3.E, U4.E, U5.E, J4.pin2, J1.pin1, J1.pin11
  N3: J2.pin1, J3.pin1
  N4: J2.pin2, J3.pin2
  N5: J2.pin3, J3.pin3
  N6: J2.pin4, J3.pin4
