# Fritzing sketch new main circuit (saved by Fritzing 0.9.3b)
stripboards: 2

parts:
  J1 = female pin header, 12 pins [form="♀ (female)"]
  J2 = female pin header, 12 pins [form="♀ (female)"]
  J3 = female pin header, 12 pins [form="♀ (female)"]
  J4 = female pin header, 12 pins [form="♀ (female)"]
  J5 = female pin header, 12 pins [form="♀ (female)"]
  J6 = female pin header, 12 pins [form="♀ (female)"]
  J7 = female pin header, 12 pins [form="♀ (female)"]
  J8 = female pin header, 24 pins [form="♀ (female)"]
  J9 = female pin header, 24 pins [form="♀ (female)"]
  Teensy1 = Teensy 3.6 (Basic)
  IC1 = IC, DIP package, 16 pins [chip_label=4051]
  IC2 = IC, DIP package, 16 pins [chip_label=4051]
  IC3 = IC, DIP package, 16 pins [chip_label=4051]
  IC4 = IC, DIP package, 16 pins [chip_label=4051]
  R1 = Resistor [tolerance=±5% resistance=10k package=THT]
  J10 = female pin header, 12 pins [form="♀ (female)"]

nets:
  GND: J1.pin1, J2.pin1, J3.pin1, J4.pin1, J5.pin1, J6.pin1, J7.pin1, J8.pin10, J9.pin24, Teensy1.GND, Teensy1.GND1, IC1.pin6, IC1.pin7, IC1.pin8, IC2.pin6, IC2.pin7, IC2.pin8, IC3.pin3, R1.Pin_0, J10.pin1
  N1: J1.pin2, J2.pin2, J3.pin2, J4.pin2, J5.pin2, J6.pin2, J7.pin2, J8.pin22, J9.pin10, Teensy1.3V3, Teensy1.3V3_1, J10.pin2
  N2: J1.pin6, J2.pin6, J3.pin6, J4.pin6, J5.pin6, J6.pin6, J7.pin6, J9.pin6, Teensy1.D27, J10.pin6
  N3: J1.pin7, J2.pin7, J3.pin7, J4.pin7, J5.pin7, J6.pin7, J7.pin7, J9.pin5, Teensy1.D28, J10.pin7
  N4: J1.pin8, J2.pin8, J3.pin8, J4.pin8, J5.pin8, J6.pin8, J7.pin8, J9.pin4, Teensy1.D29, J10.pin8
  N5: J1.pin9, J2.pin9, J3.pin9, J4.pin9, J5.pin9, J6.pin9, J7.pin9, J8.pin1, Teensy1.D33, J10.pin9
  N6: J1.pin10, J2.pin10, J3.pin10, J4.pin10, J5.pin10, J6.pin10, J7.pin10, J8.pin2, Teensy1.D34, J10.pin10
  N7: J1.pin11, J2.pin11, J3.pin11, J4.pin11, J5.pin11, J6.pin11, J7.pin11, J8.pin3, Teensy1.D35, J10.pin11
  N8: J7.pin3, IC4.pin2
  N9: J7.pin4, IC1.pin2
  N10: J7.pin5, IC2.pin2
  N11: J7.pin12, IC3.pin2
  N12: J8.pin4, Teensy1.D36
  N13: J8.pin5, Teensy1.D37
  N14: J8.pin6, Teensy1.D38
  N15: J8.pin7, Teensy1.D39
  N16: J8.pin8, Teensy1.A21/DAC0
  N17: J8.pin9, Teensy1.A22/DAC1
  N18: J8.pin11, Teensy1.D13
  N19: J8.pin12, Teensy1.A0/D14
  N20: J8.pin13, Teensy1.A1/D15
  N21: J8.pin14, Teensy1.A2/D16
  N22: J8.pin15, Teensy1.A3/D17
  N23: J8.pin16, Teensy1.A4/D18
  N24: J8.pin17, Teensy1.A5/D19
  N25: J8.pin18, Teensy1.A6/D20
  N26: J8.pin19, Teensy1.A7/D21, IC1.pin3
  N27: J8.pin20, Teensy1.A8/D22
  N28: J8.pin21, Teensy1.A9/D23
  N29: J8.pin23, Teensy1.AGND
  N30: J8.pin24, Teensy1.Vin
  N31: J9.pin1, Teensy1.D32, IC3.pin9, IC4.pin9
  N32: J9.pin2, Teensy1.D31, IC3.pin10, IC4.pin10
  N33: J9.pin3, Teensy1.D30, IC3.pin11, IC4.pin11
  N34: J9.pin7, Teensy1.D26, IC4.pin3
  N35: J9.pin8, Teensy1.D25, IC2.pin3, R1.Pin_1
  N36: J9.pin9, Teensy1.D24
  N37: J9.pin11, Teensy1.D12
  N38: J9.pin12, Teensy1.D11
  N39: J9.pin13, Teensy1.D10
  N40: J9.pin14, Teensy1.D9
  N41: J9.pin15, Teensy1.D8
  N42: J9.pin16, Teensy1.D7
  N43: J9.pin17, Teensy1.D6
  N44: J9.pin18, Teensy1.D5
  N45: J9.pin19, Teensy1.D4, IC1.pin9, IC2.pin9
  N46: J9.pin20, Teensy1.D3, IC1.pin10, IC2.pin10
  N47: J9.pin21, Teensy1.D2, IC1.pin11, IC2.pin11
  N48: J9.pin22, Teensy1.D1
  N49: J9.pin23, Teensy1.D0
  N50: IC1.pin4, J10.pin4
  N51: IC1.pin16, IC2.pin16, IC3.pin5, IC3.pin16, IC4.pin16
  N52: IC2.pin4, J10.pin5
  N53: IC3.pin4, J10.pin12
  N54: IC3.pin6, IC3.pin7, IC3.pin8, IC4.pin6, IC4.pin7, IC4.pin8

custom parts:
  Teensy 3.6 (Basic): The Teensy is a complete USB-based microcontoller development system, in a very small footprint, capable of implementing many types of projects. All programming is done via the USB port. No special programmer is needed, only a standard micro-USB cable and a PC or Macintosh with a USB port.
