# Fritzing sketch oscillator module (saved by Fritzing 0.9.3b)
stripboards: 1

parts:
  U1 = POT [package=pot_mammoth]
  IC1 = IC, DIP package, 16 pins [chip_label="4051 (send)"]
  IC2 = IC, DIP package, 16 pins [chip_label="4051 (id)"]  # not connected
  IC3 = IC, DIP package, 16 pins [chip_label="4051 (analog)"]  # not connected
  IC4 = IC, DIP package, 16 pins [chip_label="4051 (rcv)"]  # not connected
  J1 = male pin header, 12 pins [form="♂ (male)"]
  TRS1 = Audio Jack (TRS) 3.5mm [package="4Ucon 08780 [THT]"]
  TRS2 = Audio Jack (TRS) 3.5mm [package="4Ucon 08780 [THT]"]
  TRS3 = Audio Jack (TRS) 3.5mm [package="4Ucon 08780 [THT]"]
  U2 = POT [package=pot_mammoth]
  U3 = POT [package=pot_mammoth]
  J2 = male pin header, 3 pins [form="♂ (male)"]

nets:
  N1: U1.S, IC1.pin16, J1.pin11, U2.S, U3.S
  N2: U1.E, IC1.pin6, IC1.pin7, IC1.pin8, J1.pin12, U2.E, U3.E
  N3: IC1.pin2, TRS3.Tip
  N4: IC1.pin3, J1.pin1
  N5: IC1.pin4, TRS2.Tip
  N6: IC1.pin5, TRS1.Tip
  N7: IC1.pin9, J1.pin2
  N8: IC1.pin10, J1.pin3
  N9: IC1.pin11, J1.pin4
  N10: IC1.pin13, J2.pin1
  N11: IC1.pin14, J2.pin2
  N12: IC1.pin15, J2.pin3
